# Fritzing sketch desktop-thermal-printer-gadget_breadboard (saved by Fritzing 0.9.10b)
breadboards: 2

parts:
  Mod1 = Raspberry Pi Pico
  J2 = 2.1mm Barrel Jack with Terminal Block
  V1 = DC Power [voltage=5]
  Part1 = Thermal Printer
  Part2 = 2.13in Tri-Color eInk Display [part_number="Adafruit #4086"]
  J3 = Piezo Speaker
  Part3 = 2.13in Tri-Color eInk Display [part_number="Adafruit #4086"]
  S1 = Pushbutton [package=THT]
  S2 = Pushbutton [package=THT]
  S3 = Pushbutton [package=THT]
  S4 = Pushbutton [package=THT]
  R1 = Resistor [tolerance=±5% power=0.25 resistance=10000 package=THT]
  R2 = Resistor [tolerance=±5% power=0.25 resistance=10000 package=THT]
  R3 = Resistor [tolerance=±5% power=0.25 resistance=10000 package=THT]
  LED2 = RGB LED (com. anode, rbg) [package="5 mm [THT]"]

nets:
  N1: Mod1.pin_1, S3.leg0, R2.Pin_1
  N2: Mod1.pin_2, S4.leg0, R3.Pin_1
  GND: Mod1.pin_3, Mod1.pin_8, Mod1.pin_13, Mod1.pin_18, Mod1.pin_23, Mod1.pin_28, Mod1.pin_33, Mod1.pin_38, Mod1.pin_42, J2.NEG, V1.V-, Part1.GND, Part2.GND, J3.pin1, Part3.GND, S1.leg0, R1.Pin_0, R2.Pin_0, R3.Pin_0, LED2.GND, LED2.DOUT
  N3: Mod1.pin_4, J3.pin2
  N4: Mod1.pin_5, S2.leg0, R1.Pin_1
  N5: Mod1.pin_9, LED2.DIN
  N6: Mod1.pin_10, Part1.DTR
  N7: Mod1.pin_11, Part1.RXD
  N8: Mod1.pin_12, Part1.TXD
  N9: Mod1.pin_14, Part3.SCLK
  N10: Mod1.pin_15, Part3.MOSI
  N11: Mod1.pin_16, Part3.MISO
  N12: Mod1.pin_17, Part3.DISPCS
  N13: Mod1.pin_19, Part3.DC
  N14: Mod1.pin_20, Part3.SRAMCS
  N15: Mod1.pin_21, Part2.MISO
  N16: Mod1.pin_22, Part2.DISPCS
  N17: Mod1.pin_24, Part2.SCLK
  N18: Mod1.pin_25, Part2.MOSI
  N19: Mod1.pin_26, Part3.RESET
  N20: Mod1.pin_27, Part2.RESET
  N21: Mod1.pin_29, Part2.SRAMCS
  N22: Mod1.pin_30, S1.leg1
  N23: Mod1.pin_31, Part2.DC
  N24: Mod1.pin_32, Part2.SDCS
  N25: Mod1.pin_34, Part3.SDCS
  VIN: Mod1.pin_36, Part2.VIN, Part3.VIN, S2.leg1, S3.leg1, S4.leg1
  N26: Mod1.pin_39, J2.POS, V1.V+, Part1.VH, LED2.VDD

custom parts:
  Raspberry Pi Pico: Raspberry Pi Pico. Based around the RP2040 microcontroller the Pico is a low cost microcontroller device bringing Raspberry Pi quality, cost, and easy of use to the microcontroller space. Jan 2021, Split part in to two versions: tht (this one) and SMD. This one will drill holes for a .1 in header in pcb to allow plugging in the module as well as providing pads to solder the module to the top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
  Thermal Printer: Description: This is a thermal printer like you would find on a cash register or adding machine. It will print simple strings passed to it via TTL serial, bitmap images (poorly) and it even generates several different formats of barcodes! The thermal printer takes 2.25" (57mm) wide thermal paper with a max roll diameter of 1.5" (39mm). Thermal paper is inexpensive and commonly found in most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
  RGB LED (com. anode, rbg): A 5mm tri-color LED with red, green and blue inside. Pin order: red - com. anode - blue - green
